# Fritzing sketch fritzing_sketch (saved by Fritzing 0.9.5d)
breadboards: 1

parts:
  J1 = STM32 Nucleo boards
  Part1 = Arduino USB Host Shield
  JP2 = USB_MICROB_PLUG [package=micro-b-th]
  OLED1 = OLED 128x64 I2C Monochrome Display
  S1 = SWITCH-MOMENTARY-2 [package=tactile_switch_smd]
  S2 = SWITCH-MOMENTARY-2 [package=tactile_switch_smd]
  S3 = SWITCH-MOMENTARY-2 [package=tactile_switch_smd]

nets:
  N1: J1.PA12, JP2.D+
  N2: J1.PA11, JP2.ID
  N3: J1.D8, Part1.GPX
  N4: J1.D9_PWM, Part1.INT
  N5: J1.D10_PWM/SS, Part1.SS
  N6: J1.D11_PWM/MOSI, Part1.MOSI
  N7: J1.D12/MISO, Part1.MISO
  N8: J1.D13/SCK, Part1.SCK
  GND: J1.GND, Part1.GND
  N9: J1.A4/SDA, OLED1.SDA
  N10: J1.A5/SCL, OLED1.SCL
  N11: J1.D5_PWM, S3.2
  N12: J1.D6_PWM, S2.2
  N13: J1.D7, S1.2
  3V3: J1.3V3, Part1.3.3V-ARDUINO, JP2.VCC, OLED1.VDD
  N14: J1.5V, Part1.5V-ARDUINO
  N15: J1.AGND, OLED1.GND
  N16: S1.1, S2.1, S3.1

notes:
  For micro usb:
  Orange wire is Data+
  Blue Wire is Data-
  Micro usb above connects to XBOX
  SCK should be SCL
  Bluetooth dongle plugs here
